# Fritzing sketch Microview ideas Manual Layout R33 0v1 (saved by Fritzing 0.9.2b)
circuit board: 5.66585cm x 9.77512cm

parts:
  MicroView = MicroView [part_number=MicroView package="16pin wide"]
  Wi-Fi_Module = XBee
  MicroView_Breakout = female pin header, 16 pins [form="♀ (female)"]
  1 = Pad [width=3.03585894193728 height=6.87308646450179 connect=center]
  C2 = Capacitor Polarized [package=cpol-radial-10uf-25v]
  C1 = Capacitor Polarized [package=cpol-radial-10uf-25v]
  Reset = Pushbutton [package="[THT]"]
  TX = male pin header, 2 pins [form="♂ (male)"]
  RX = male pin header, 2 pins [form="♂ (male)"]
  Reset_2 = Pushbutton [package="[THT]"]
  1_2 = single row smd female pin header, 1 pin [form="♀ (female)"]
  2 = single row smd female pin header, 1 pin [form="♀ (female)"]
  3 = single row smd female pin header, 1 pin [form="♀ (female)"]
  12 = single row smd female pin header, 1 pin [form="♀ (female)"]
  U2 = PNP-Transistor [part_number=MCP1700 package="TO92 [THT]"]
  3_2 = Pad [width=3.03585894193728 height=6.87308646450179 connect=center]
  4 = Pad [width=3.03585894193728 height=6.87308646450179 connect=center]  # not connected
  2_2 = Pad [width=3.03585894193728 height=6.87308646450179 connect=center]
  5 = Pad [width=3.03585894193728 height=6.87308646450179 connect=center]  # not connected
  6 = Pad [width=3.03585894193728 height=6.87308646450179 connect=center]  # not connected
  7 = Pad [width=3.03585894193728 height=6.87308646450179 connect=center]  # not connected
  8 = Pad [width=3.03585894193728 height=6.87308646450179 connect=center]  # not connected
  9 = Pad [width=3.03585894193728 height=6.87308646450179 connect=center]  # not connected
  10 = Pad [width=3.03585894193728 height=6.87308646450179 connect=center]  # not connected
  11 = Pad [width=3.03585894193728 height=6.87308646450179 connect=center]  # not connected
  12_2 = Pad [width=3.03585894193728 height=6.87308646450179 connect=center]
  VIN = 2.1mm DC Barrel Jack
  N = Pad [width=3.03585894193728 height=6.87308646450179 connect=center]
  B = Pad [width=3.03585894193728 height=6.87308646450179 connect=center]
  C = Pad [width=3.03585894193728 height=6.87308646450179 connect=center]
  D = Pad [width=3.03585894193728 height=6.87308646450179 connect=center]
  E = Pad [width=3.03585894193728 height=6.87308646450179 connect=center]
  F = Pad [width=3.03585894193728 height=6.87308646450179 connect=center]
  H = Pad [width=3.03585894193728 height=6.87308646450179 connect=center]
  J = Pad [width=3.03585894193728 height=6.87308646450179 connect=center]
  K = Pad [width=3.03585894193728 height=6.87308646450179 connect=center]
  L = Pad [width=3.03585894193728 height=6.87308646450179 connect=center]
  M = Pad [width=3.03585894193728 height=6.87308646450179 connect=center]
  D_2 = single row smd female pin header, 1 pin [form="♀ (female)"]
  M_2 = single row smd female pin header, 1 pin [form="♀ (female)"]
  A = single row smd female pin header, 1 pin [form="♀ (female)"]
  H_2 = single row smd female pin header, 1 pin [form="♀ (female)"]
  F_2 = single row smd female pin header, 1 pin [form="♀ (female)"]
  C_2 = single row smd female pin header, 1 pin [form="♀ (female)"]
  Reset_3 = Pushbutton [package="[THT]"]
  E_2 = single row smd female pin header, 1 pin [form="♀ (female)"]
  L_2 = single row smd female pin header, 1 pin [form="♀ (female)"]
  B_2 = single row smd female pin header, 1 pin [form="♀ (female)"]
  J_2 = single row smd female pin header, 1 pin [form="♀ (female)"]
  K_2 = single row smd female pin header, 1 pin [form="♀ (female)"]
  N_2 = single row smd female pin header, 1 pin [form="♀ (female)"]
  4116R-1-331LF = IC, DIP package, 16 pins [chip_label=IC]
  A_2 = Pad [width=3.03585894193728 height=6.87308646450179 connect=center]  # not connected

nets:
  N1: MicroView.RESET, MicroView_Breakout.pin1, Reset_2.Pin_1, Reset_2.Pin_2
  RTS: MicroView.A5, MicroView_Breakout.pin2, 4116R-1-331LF.pin10
  DTR: MicroView.A4, MicroView_Breakout.pin3, 4116R-1-331LF.pin11
  RI: MicroView.A3, MicroView_Breakout.pin4, 4116R-1-331LF.pin12
  DCD: MicroView.A2, MicroView_Breakout.pin5, 4116R-1-331LF.pin13
  CTS: MicroView.A1, MicroView_Breakout.pin6, 4116R-1-331LF.pin14
  DSR: MicroView.A0, MicroView_Breakout.pin7, 4116R-1-331LF.pin15
  N2: MicroView.GND, MicroView_Breakout.pin8
  N3: MicroView.RXD, MicroView_Breakout.pin9
  N4: MicroView.TXD, MicroView_Breakout.pin10
  N5: MicroView.D2, Wi-Fi_Module.pin2, MicroView_Breakout.pin11, RX.pin1
  N6: MicroView.D3, Wi-Fi_Module.pin3, MicroView_Breakout.pin12, TX.pin1
  TxD: MicroView.D5, MicroView_Breakout.pin13, TX.pin2, 4116R-1-331LF.pin16
  RxD: MicroView.D6, MicroView_Breakout.pin14, RX.pin2, 4116R-1-331LF.pin9
  5V: MicroView.5V, MicroView_Breakout.pin15, 2.pin1, U2.B, 2_2.pad
  VIN: MicroView.Vin, MicroView_Breakout.pin16, VIN.center
  3.3V: Wi-Fi_Module.VCC, C2.+, C1.+, U2.C
  N7: Wi-Fi_Module.pin5, Reset.Pin_1
  GND: Wi-Fi_Module.GND, C2.-, C1.-, Reset.Pin_3, Reset.Pin_4, Reset_2.Pin_3, Reset_2.Pin_4, 12.pin1, U2.E, 12_2.pad, VIN.switch, VIN.sleeve, N.pad, A.pin1, Reset_3.Pin_3, Reset_3.Pin_4, N_2.pin1
  N8: 1.pad, 1_2.pin1
  RESET64: 3.pin1, 3_2.pad, Reset_3.Pin_1, Reset_3.Pin_2
  N9: B.pad, C.pad, C_2.pin1, B_2.pin1, 4116R-1-331LF.pin8
  N10: D.pad, D_2.pin1, 4116R-1-331LF.pin7
  N11: E.pad, E_2.pin1, 4116R-1-331LF.pin6
  N12: F.pad, F_2.pin1, 4116R-1-331LF.pin5
  N13: H.pad, H_2.pin1, 4116R-1-331LF.pin4
  N14: J.pad, J_2.pin1
  N15: K.pad, K_2.pin1, 4116R-1-331LF.pin3
  N16: L.pad, L_2.pin1, 4116R-1-331LF.pin2
  N17: M.pad, M_2.pin1, 4116R-1-331LF.pin1

notes:
  RESET
  A5 SCL
  A4 SDA
  A3
  A2
  A1
  A0
  GND
  D0 RXD
  D2
  D3
  D5
  D6
  +5V
  VIN
  Top
  1
  16
  Commodore 64 - MicroView - Wi-Fi Cart
  Leif Bloomquist  2015  0v1
  Wi-Fi
  Direct
  Signals to C64 User Port
  TX
  RX
  Jumpers to connect C64 directly to RN-XV if MicroView not present
  Actual C64 User Port
  MicroView
  RN-XV
  Current Limiting Resistor Network
  Note pinout swapped!
  See MCP-1700 Datasheet
  Assumptions:
  C64 5V is clean/stable enough to use as 5V directly (not through VIN)
  C64
  D1 TXD
  -RxD-
  -RTS-
  -DTR-
  -RI-
  -DCD-
  -CTS-
  -DSR-
  -TxD-
  U1

custom parts:
  MicroView: MicroView - Chip-sized Arduino with OLED display.
  2.1mm DC Barrel Jack: 2.1mm DC Barrel Jack with Thru-Hole Connectors (breadboardable)
