# Fritzing sketch Microview SoundScope R4_0v1 (saved by Fritzing 0.9.2b)
circuit board: 2.41237cm x 2.28573cm
breadboards: 1

parts:
  MicroView_(Top) = MicroView [part_number=MicroView package="16pin wide"]
  Power = Header 2 [package=jst-2-pth-ns]
  Audio = Header 3 [package=jst-3-pth]

nets:
  N1: MicroView_(Top).A3, Audio.1
  GND: MicroView_(Top).GND, Power.1, Audio.2
  N2: MicroView_(Top).5V, Audio.3
  N3: MicroView_(Top).Vin, Power.2

notes:
  AUD
  GND
  VCC
  2015 0v2
  Schema Factor
  Sound Scope
  MicroView

custom parts:
  MicroView: MicroView - Chip-sized Arduino with OLED display.
