# Fritzing sketch Microview ideas R10 (saved by Fritzing 0.9.2b)

parts:
  MicroView = MicroView [part_number=MicroView package="16pin wide"]
  RN-XV = XBee
  Buffer_IC_TBD = IC, DIP package, 20 pins [chip_label="Octal Buffer"]  # not connected
  MicroView_Breakout = female pin header, 16 pins [form="♀ (female)"]
  1 = Pad [width=3.03585894193728 height=6.87308646450179 connect=center]  # not connected
  C2 = Capacitor Polarized [package=cpol-radial-10uf-25v]
  C1 = Capacitor Polarized [package=cpol-radial-10uf-25v]
  RESET = Pushbutton [package="[THT]"]
  TX = male pin header, 2 pins [form="♂ (male)"]
  RX = male pin header, 2 pins [form="♂ (male)"]
  RESET_2 = Pushbutton [package="[THT]"]
  1_2 = single row smd female pin header, 1 pin [form="♀ (female)"]
  2 = single row smd female pin header, 1 pin [form="♀ (female)"]
  3 = single row smd female pin header, 1 pin [form="♀ (female)"]
  12 = single row smd female pin header, 1 pin [form="♀ (female)"]
  A = single row smd female pin header, 1 pin [form="♀ (female)"]
  K = single row smd female pin header, 1 pin [form="♀ (female)"]  # not connected
  F = single row smd female pin header, 1 pin [form="♀ (female)"]  # not connected
  H = single row smd female pin header, 1 pin [form="♀ (female)"]  # not connected
  L = single row smd female pin header, 1 pin [form="♀ (female)"]  # not connected
  J = single row smd female pin header, 1 pin [form="♀ (female)"]  # not connected
  D = single row smd female pin header, 1 pin [form="♀ (female)"]  # not connected
  B = single row smd female pin header, 1 pin [form="♀ (female)"]
  M = single row smd female pin header, 1 pin [form="♀ (female)"]  # not connected
  C = single row smd female pin header, 1 pin [form="♀ (female)"]
  E = single row smd female pin header, 1 pin [form="♀ (female)"]  # not connected
  N = single row smd female pin header, 1 pin [form="♀ (female)"]
  U1 = PNP-Transistor [part_number=MCP1700 package="TO92 [THT]"]
  3_2 = Pad [width=3.03585894193728 height=6.87308646450179 connect=center]  # not connected
  4 = Pad [width=3.03585894193728 height=6.87308646450179 connect=center]  # not connected
  2_2 = Pad [width=3.03585894193728 height=6.87308646450179 connect=center]  # not connected
  5 = Pad [width=3.03585894193728 height=6.87308646450179 connect=center]  # not connected
  6 = Pad [width=3.03585894193728 height=6.87308646450179 connect=center]  # not connected
  7 = Pad [width=3.03585894193728 height=6.87308646450179 connect=center]  # not connected
  8 = Pad [width=3.03585894193728 height=6.87308646450179 connect=center]  # not connected
  9 = Pad [width=3.03585894193728 height=6.87308646450179 connect=center]  # not connected
  10 = Pad [width=3.03585894193728 height=6.87308646450179 connect=center]  # not connected
  11 = Pad [width=3.03585894193728 height=6.87308646450179 connect=center]  # not connected
  12_2 = Pad [width=3.03585894193728 height=6.87308646450179 connect=center]  # not connected
  5V = 2.1mm DC Barrel Jack

nets:
  N1: MicroView.RESET, MicroView_Breakout.pin1, RESET_2.Pin_1, RESET_2.Pin_2
  N2: MicroView.A5, MicroView_Breakout.pin2
  RTS: MicroView.A4, MicroView_Breakout.pin3
  DTR: MicroView.A3, MicroView_Breakout.pin4
  RI: MicroView.A2, MicroView_Breakout.pin5
  DCD: MicroView.A1, MicroView_Breakout.pin6
  DSR: MicroView.A0, MicroView_Breakout.pin7
  N3: MicroView.GND, MicroView_Breakout.pin8
  N4: MicroView.RXD, MicroView_Breakout.pin9
  N5: MicroView.TXD, MicroView_Breakout.pin10
  N6: MicroView.D2, MicroView_Breakout.pin11
  N7: MicroView.D3, RN-XV.pin3, MicroView_Breakout.pin12, TX.pin2
  TxD: MicroView.D5, MicroView_Breakout.pin13, TX.pin1
  RxD: MicroView.D6, MicroView_Breakout.pin14, RX.pin1
  5V: MicroView.5V, MicroView_Breakout.pin15, 2.pin1, U1.E, 5V.center
  N8: MicroView.Vin, MicroView_Breakout.pin16
  3.3V: RN-XV.VCC, U1.C
  N9: RN-XV.pin2, RX.pin2
  N10: RN-XV.pin5, RESET.Pin_1
  GND: RN-XV.GND, C2.-, C1.-, RESET.Pin_3, RESET.Pin_4, RESET_2.Pin_3, RESET_2.Pin_4, 1_2.pin1, 12.pin1, A.pin1, N.pin1, U1.B, 5V.switch, 5V.sleeve
  N11: C2.+, C1.+
  RESET64: 3.pin1
  N12: B.pin1, C.pin1

notes:
  RESET
  A5 SCL
  A4 SDA
  A3
  A2
  A1
  A0
  GND
  D0 RXD
  D1 TXD
  D2
  D3
  D5
  D6
  +5V
  VIN
  ^ Top ^
  1
  16
  Commodore 64 - MicroView - WiFi Cart
  Leif Bloomquist  2015  0v1
  RN-XV
  Direct
  Signals to C64 User Port
  TX
  RX
  Jumpers to connect C64 directly to RN-XV if MicroView not present
  Actual C64 User Port

custom parts:
  MicroView: MicroView - Chip-sized Arduino with OLED display.
  2.1mm DC Barrel Jack: 2.1mm DC Barrel Jack with Thru-Hole Connectors (breadboardable)
