# Fritzing sketch MicroView SoundScope_Electret_R11_0v2 (saved by Fritzing 0.9.2b)
circuit board: 2.41237cm x 2.28573cm
breadboards: 1

parts:
  MicroView_(Top) = MicroView [part_number=MicroView package="16pin wide"]
  Power = Header 2 [package=jst-2-pth-ns]
  BOB-09964 = Breakout Board for Electret Microphone

nets:
  N1: MicroView_(Top).A3, BOB-09964.VCC
  GND: MicroView_(Top).GND, Power.1, BOB-09964.GND
  5V: MicroView_(Top).5V, BOB-09964.AUD
  N2: MicroView_(Top).Vin, Power.2

notes:
  AUD
  GND
  VCC
  2015 0v2
  Schema Factor
  Sound Scope
  MicroView
  VCC and AUD are
  swapped on the PCB View, so swapped here to correct.

custom parts:
  MicroView: MicroView - Chip-sized Arduino with OLED display.
